// Logisim project 16bit-cpu.circ as structural Verilog: 4 circuits, main circuit cpu
module cpu (
  input  in_1
);

  wire clk, en_flag, load, load_alu, load_imm, load_mem, set_instr, store, undriven;
  wire [2:0] alu_op, reg_a, reg_b, reg_n;
  wire [3:0] alu_1_zero, bit_extender_1_out, bit_extender_2_out, bit_extender_3_out, bit_extender_4_out,
       flag_reg;
  wire [7:0] alu_res, byte_out, controlled_buffer_1_out, Memory_dout, Program_Count_q, reg_out,
       registers_1_out_b;
  wire [15:0] Instruction_Register_q, Program_ROM_data;

  Clock clock_1 (.out(clk));
  RAM Memory (.addr(byte_out), .we(store), .oe(load_mem), .clk(clk), .din(reg_out), .dout(Memory_dout));
  Counter Program_Count (
    .load(set_instr), .clk(clk), .D(byte_out), .Q(Program_Count_q));  // open: clr, up, count, carry
  Hex_Digit_Display hex_digit_display_1 (.value(bit_extender_1_out));  // open: dp
  assign bit_extender_1_out = {{1{1'b0}}, alu_op};  // Bit_Extender bit_extender_1
  Hex_Digit_Display hex_digit_display_2 (.value(bit_extender_2_out));  // open: dp
  assign bit_extender_2_out = {{1{1'b0}}, reg_n};  // Bit_Extender bit_extender_2
  ROM #(.dataWidth(16)) Program_ROM (.addr(Program_Count_q), .data(Program_ROM_data));
  Hex_Digit_Display hex_digit_display_3 (.value(byte_out[7:4]));  // open: dp
  Hex_Digit_Display hex_digit_display_4 (.value(byte_out[3:0]));  // open: dp
  assign controlled_buffer_1_out = load_mem ? Memory_dout : 8'bz;  // Controlled_Buffer controlled_buffer_1
  assign controlled_buffer_1_out = load_alu ? alu_res : 8'bz;  // Controlled_Buffer controlled_buffer_2
  assign controlled_buffer_1_out = load_imm ? byte_out : 8'bz;  // Controlled_Buffer controlled_buffer_3
  Hex_Digit_Display hex_digit_display_5 (.value(bit_extender_3_out));  // open: dp
  assign bit_extender_3_out = {{1{1'b0}}, reg_a};  // Bit_Extender bit_extender_3
  Register #(.width(16)) Instruction_Register (
    .D(Program_ROM_data), .en(1'b1), .clk(clk), .Q(Instruction_Register_q));  // open: clr
  Hex_Digit_Display hex_digit_display_6 (.value(bit_extender_4_out));  // open: dp
  assign bit_extender_4_out = {{1{1'b0}}, reg_b};  // Bit_Extender bit_extender_4
  Registers registers_1 (
    .clk(clk), .in_val(controlled_buffer_1_out), .write(load), .reg_num(reg_n), .clr_reg(in_1), .Ra(reg_a),
    .Rb(reg_b), .out_a(reg_out), .out_b(registers_1_out_b));
  LED overflow (.in(flag_reg[3]));
  Control_Unit control_unit_1 (
    .instruction(Instruction_Register_q), .flags(flag_reg), .load(load), .store(store), .en_flag(en_flag),
    .load_mem(load_mem), .load_imm(load_imm), .load_alu(load_alu), .reg_n(reg_n), .byte_out(byte_out),
    .reg_b(reg_b), .reg_a(reg_a), .alu_op(alu_op), .set_instr(set_instr));
  LED carry (.in(flag_reg[2]));
  Controlled_Buffer #(.width(8)) controlled_buffer_4 (.en(undriven));  // open: in, out
  LED zero (.in(flag_reg[0]));
  LED negative (.in(flag_reg[1]));
  Hex_Digit_Display hex_digit_display_7 (.value(alu_res[7:4]));  // open: dp
  Hex_Digit_Display hex_digit_display_8 (.value(alu_res[3:0]));  // open: dp
  ALU alu_1 (
    .in_a(reg_out), .in_b(registers_1_out_b), .op(alu_op), .carry_out(alu_1_zero[2]), .out_val(alu_res),
    .neg(alu_1_zero[1]), .zero(alu_1_zero[0]), .overflow(alu_1_zero[3]));
  Register #(.width(4)) register_1 (.D(alu_1_zero), .en(en_flag), .clk(clk), .Q(flag_reg), .clr(1'b0));

  // Notes on the sheet:
  //   contents of Program_ROM (hex, n*v repeats v):
  //   1a0b 1905 1b01 304b 500a 4403
endmodule

module Registers (
  input  [7:0] in_val,
  input  clk,
  input  [2:0] Ra,
  input  write,
  input  [2:0] reg_num,
  input  [2:0] Rb,
  input  clr_reg,
  output [7:0] out_a,
  output [7:0] out_b
);

  wire decoder_1_out1, decoder_1_out2, decoder_1_out3, decoder_1_out4, decoder_1_out5, decoder_1_out6,
       decoder_1_out7;
  wire [7:0] register_1_q, register_2_q, register_3_q, register_4_q, register_5_q, register_6_q, register_7_q;

  Decoder #(.select(3)) decoder_1 (
    .out1(decoder_1_out1), .out2(decoder_1_out2), .out3(decoder_1_out3), .out4(decoder_1_out4),
    .out5(decoder_1_out5), .out6(decoder_1_out6), .out7(decoder_1_out7), .sel(reg_num), .en(write));  // open: out0
  Register register_1 (.D(in_val), .en(decoder_1_out1), .clk(clk), .Q(register_1_q), .clr(clr_reg));
  Register register_2 (.D(in_val), .en(decoder_1_out2), .clk(clk), .Q(register_2_q), .clr(clr_reg));
  Register register_3 (.D(in_val), .en(decoder_1_out3), .clk(clk), .Q(register_3_q), .clr(clr_reg));
  Register register_4 (.D(in_val), .en(decoder_1_out4), .clk(clk), .Q(register_4_q), .clr(clr_reg));
  Register register_5 (.D(in_val), .en(decoder_1_out5), .clk(clk), .Q(register_5_q), .clr(clr_reg));
  Register register_6 (.D(in_val), .en(decoder_1_out6), .clk(clk), .Q(register_6_q), .clr(clr_reg));
  Register register_7 (.D(in_val), .en(decoder_1_out7), .clk(clk), .Q(register_7_q), .clr(clr_reg));
  Multiplexer #(.select(3), .width(8)) multiplexer_1 (
    .in0({8{1'b0}}), .in1(register_1_q), .in2(register_2_q), .in3(register_3_q), .in4(register_4_q),
    .in5(register_5_q), .in6(register_6_q), .in7(register_7_q), .out(out_a), .sel(Ra));
  Multiplexer #(.select(3), .width(8)) multiplexer_2 (
    .in0({8{1'b0}}), .in1(register_1_q), .in2(register_2_q), .in3(register_3_q), .in4(register_4_q),
    .in5(register_5_q), .in6(register_6_q), .in7(register_7_q), .out(out_b), .sel(Rb));
endmodule

module ALU (
  input  [7:0] in_a,
  input  [7:0] in_b,
  input  [2:0] op,
  output carry_out,
  output [7:0] out_val,
  output zero,
  output neg,
  output overflow
);

  wire adder_1_cout, subtractor_1_bout, xnor_1_out, xor_2_out;
  wire [7:0] adder_1_out, and_1_out, not_1_out, or_1_out, shifter_1_out, shifter_2_out, subtractor_1_out,
       xor_1_out;

  Adder adder_1 (.a(in_a), .b(in_b), .out(adder_1_out), .cout(adder_1_cout));  // open: cin
  Subtractor subtractor_1 (.a(in_b), .b(in_a), .out(subtractor_1_out), .bout(subtractor_1_bout));  // open: bin
  assign and_1_out = in_a & in_b;  // AND_Gate and_1, 8 bits wide
  assign or_1_out = in_a | in_b;  // OR_Gate or_1, 8 bits wide
  assign xor_1_out = in_a ^ in_b;  // XOR_Gate xor_1, 8 bits wide
  Shifter shifter_1 (.in(in_a), .\dist (3'b001), .out(shifter_1_out));
  Shifter #(.shift("lr")) shifter_2 (.in(in_a), .\dist (3'b001), .out(shifter_2_out));
  assign not_1_out = ~in_a;  // NOT_Gate not_1, 8 bits wide
  Multiplier multiplier_1 ();  // open: a, b, out, cin, cout
  xnor xnor_1 (xnor_1_out, in_a[0], in_b[0]);
  or or_2 (carry_out, adder_1_cout, subtractor_1_bout);
  Multiplexer #(.select(3), .width(8)) multiplexer_1 (
    .in0(adder_1_out), .in1(subtractor_1_out), .in2(and_1_out), .in3(or_1_out), .in4(xor_1_out),
    .in5(shifter_1_out), .in6(shifter_2_out), .in7(not_1_out), .out({neg, out_val[6:0]}), .sel(op));
  nor nor_1 (zero, out_val[0], out_val[1], out_val[2], out_val[3], out_val[4], out_val[5], out_val[6], neg);
  xor xor_2 (xor_2_out, neg, in_a[0]);
  and and_2 (overflow, xor_2_out, xnor_1_out);

  assign out_val[7] = neg;
endmodule

module Control_Unit (
  input  [15:0] instruction,
  input  [3:0] flags,
  output load,
  output store,
  output en_flag,
  output load_mem,
  output load_imm,
  output load_alu,
  output [2:0] reg_n,
  output [7:0] byte_out,
  output [2:0] reg_b,
  output [2:0] reg_a,
  output [2:0] alu_op,
  output set_instr
);

  wire controlled_buffer_1_out, controlled_buffer_2_out, controlled_buffer_3_out, controlled_buffer_5_out,
       decoder_1_out1, decoder_1_out4, nor_1_out, or_1_out, or_2_out, or_3_out, or_4_out;

  Decoder #(.enable("false"), .select(4)) decoder_1 (
    .out1(decoder_1_out1), .out2(store), .out3(load_alu), .out4(decoder_1_out4), .out5(en_flag),
    .sel(instruction[15:12]));  // open: out0, out6, out7, out8, out9, out10, out11, out12, out13, out14, out15
  assign controlled_buffer_1_out = instruction[8] ? flags[3] : 1'bz;  // Controlled_Buffer controlled_buffer_1
  assign controlled_buffer_2_out = instruction[9] ? flags[2] : 1'bz;  // Controlled_Buffer controlled_buffer_2
  assign controlled_buffer_3_out = instruction[10] ? flags[1] : 1'bz;  // Controlled_Buffer controlled_buffer_3
  or or_1 (or_1_out, load_alu, en_flag);
  assign reg_b = or_1_out ? instruction[2:0] : 3'bz;  // Controlled_Buffer controlled_buffer_4
  assign controlled_buffer_5_out = instruction[11] ? flags[0] : 1'bz;  // Controlled_Buffer controlled_buffer_5
  or or_2 (or_2_out, load_alu, en_flag);
  assign reg_a = or_2_out ? instruction[5:3] : 3'bz;  // Controlled_Buffer controlled_buffer_6
  assign reg_n = load_alu ? instruction[8:6] : 3'bz;  // Controlled_Buffer controlled_buffer_7
  assign alu_op = en_flag ? 3'b001 : 3'bz;  // Controlled_Buffer controlled_buffer_8
  nor nor_1 (nor_1_out, instruction[8], instruction[9], instruction[10], instruction[11]);
  and and_1 (load_mem, decoder_1_out1, ~instruction[11]);  // AND_Gate
  and and_2 (load_imm, decoder_1_out1, instruction[11]);
  assign reg_a = store ? instruction[10:8] : 3'bz;  // Controlled_Buffer controlled_buffer_9
  assign alu_op = load_alu ? instruction[11:9] : 3'bz;  // Controlled_Buffer controlled_buffer_10
  or or_3 (or_3_out, nor_1_out, controlled_buffer_1_out, controlled_buffer_2_out, controlled_buffer_3_out, controlled_buffer_5_out);
  and and_3 (set_instr, decoder_1_out4, or_3_out);
  or or_4 (or_4_out, load_mem, load_imm, decoder_1_out4, store);
  assign byte_out = or_4_out ? instruction[7:0] : 8'bz;  // Controlled_Buffer controlled_buffer_11
  or or_5 (load, decoder_1_out1, load_alu);
  assign reg_n = decoder_1_out1 ? instruction[10:8] : 3'bz;  // Controlled_Buffer controlled_buffer_12
endmodule
